# Fritzing sketch diagram (saved by Fritzing 1.0.4)
breadboards: 1

parts:
  Part1 = Arduino Uno (Rev3) - ICSP
  hand = Basic Servo
  top = Basic Servo
  middle = Basic Servo
  bottom = Basic Servo
  base = Basic Servo
  Part2 = Breadboard Power Supply Board SMD
  HC-08 = Bluetooth HC-05 Macho
  R2 = Resistor [tolerance=±5% power=0.25W resistance=1k package=THT]
  R3 = Resistor [tolerance=±5% power=0.25W resistance=2.2k package=THT]

nets:
  GND: Part1.GND, hand.gnd, top.gnd, middle.gnd, bottom.gnd, base.gnd, Part2.GND, HC-08.GND, R3.Pin_1
  N1: Part1.D8, R2.Pin_1, R3.Pin_0
  N2: Part1.D9_PWM, bottom.pulse
  N3: Part1.D10_PWM/SS, base.pulse
  N4: Part1.D3_PWM, hand.pulse
  N5: Part1.D5_PWM, top.pulse
  N6: Part1.D6_PWM, middle.pulse
  N7: Part1.D7, HC-08.TXD
  VCC: Part1.VIN, hand.vcc, top.vcc, middle.vcc, bottom.vcc, base.vcc, Part2.VCC, HC-08.VCC
  N8: HC-08.RXD, R2.Pin_0
